// Logisim project cpu.circ as structural Verilog: 5 circuits, main circuit CPU
module CPU (
  output [47:0] cpu_out,
  output halt
);

  wire ALU_instruc, and_1_out, and_2_out, Branch, C, clk, ConditionCool, EQ, GE, GT, IR_WE, LE, Load, LT, N,
       NE, or_1_out, PC_WE, RA_WE, RB_WE, RD_WE, reset, RF_WE, RW_WE, RZ_WE, Store, V, Z;
  wire [2:0] multiplexer_2_out, multiplexer_4_out;
  wire [15:0] A, adder_1_out, ArithmeticLogicUnit_c, B, bit_extender_1_out, bit_extender_2_out, C_out,
       InsMem_data, multiplexer_1_out, multiplexer_3_out, multiplexer_5_out, RA_q, RAM_out, RB, RD;

  Clock u_clk (.out(clk));
  Button u_reset (.out(reset));
  assign bit_extender_1_out = {{13{cpu_out[25]}}, cpu_out[25:23]};  // Bit_Extender bit_extender_1
  Multiplexer #(.width(16)) multiplexer_1 (
    .in0(16'h1), .in1(bit_extender_1_out), .out(multiplexer_1_out), .sel(and_1_out));
  and and_1 (and_1_out, Branch, ConditionCool, RD_WE);
  Adder #(.width(16)) adder_1 (.a(cpu_out[47:32]), .b(multiplexer_1_out), .out(adder_1_out));  // open: cin, cout
  Multiplexer #(.width(3)) multiplexer_2 (
    .in0(cpu_out[18:16]), .in1(cpu_out[25:23]), .out(multiplexer_2_out), .sel(Store));
  Register #(.width(16)) PC (.D(adder_1_out), .en(PC_WE), .clk(clk), .Q(cpu_out[47:32]), .clr(reset));
  RegisterFile register_file (
    .Addr_A(cpu_out[22:20]), .Addr_B(multiplexer_2_out), .Addr_C(cpu_out[25:23]), .we(RF_WE), .clk(clk),
    .reset(reset), .C(C_out), .A(A), .B(B));
  FSM F_S_M (
    .clk(clk), .reset(reset), .OPCODE(cpu_out[31:30]), .ConditionCool(ConditionCool), .IR_WE(IR_WE),
    .PC_WE(PC_WE), .RA_WE(RA_WE), .RB_WE(RB_WE), .RZ_WE(RZ_WE), .RD_WE(RD_WE), .RW_WE(RW_WE), .RF_WE(RF_WE));
  ROM #(.addrWidth(16), .dataWidth(16)) InsMem (.addr(cpu_out[47:32]), .data(InsMem_data));
  Register #(.width(16)) RA (.D(A), .en(RA_WE), .clk(clk), .Q(RA_q), .clr(reset));
  Register #(.width(16)) u_RB (.D(B), .en(RB_WE), .clk(clk), .Q(RB), .clr(reset));
  Register #(.width(16)) IR (.D(InsMem_data), .en(IR_WE), .clk(clk), .Q(cpu_out[31:16]), .clr(reset));
  assign bit_extender_2_out = {{12{cpu_out[19]}}, cpu_out[19:16]};  // Bit_Extender bit_extender_2
  Multiplexer #(.width(16)) multiplexer_3 (.in0(RB), .in1(bit_extender_2_out), .out(multiplexer_3_out), .sel(or_1_out));
  or or_1 (or_1_out, cpu_out[26], Store);
  Comparator #(.width(16)) comparator_1 (.a(cpu_out[31:16]), .b(16'h4380), .eq(halt));  // open: gt, lt
  Multiplexer #(.width(3)) multiplexer_4 (.in0(cpu_out[29:27]), .in1(3'b001), .out(multiplexer_4_out), .sel(Branch));
  ALU ArithmeticLogicUnit (
    .A(RA_q), .B(multiplexer_3_out), .fun(multiplexer_4_out), .negative(N), .C(ArithmeticLogicUnit_c),
    .zero(Z), .carry(C), .overflow(V));
  Register #(.width(16)) u_RD (.D(RB), .en(RD_WE), .clk(clk), .Q(RD), .clr(reset));
  Decoder #(.enable("false"), .select(2)) decoder_1 (
    .out0(ALU_instruc), .out1(Branch), .out2(Load), .out3(Store), .sel(cpu_out[31:30]));
  Register #(.width(16)) RZ (.D(ArithmeticLogicUnit_c), .en(RZ_WE), .clk(clk), .Q(cpu_out[15:0]), .clr(reset));
  and and_2 (and_2_out, RW_WE, Store);
  Multiplexer #(.width(16)) multiplexer_5 (.in0(cpu_out[15:0]), .in1(RAM_out), .out(multiplexer_5_out), .sel(Load));
  RAM #(.addrWidth(16), .dataWidth(16), .enables("line")) ram_1 (
    .addr(cpu_out[15:0]), .we(and_2_out), .clk(clk), .din(RD), .dout(RAM_out));
  Register #(.width(16)) RW (.D(multiplexer_5_out), .en(RW_WE), .clk(clk), .Q(C_out), .clr(reset));
  Comparator #(.width(1)) comparator_2 (.a(Z), .b(1'b1), .eq(EQ));  // open: gt, lt
  Comparator #(.width(1)) comparator_3 (.a(Z), .b(1'b0), .eq(NE));  // open: gt, lt
  xor xor_1 (LT, N, V);
  or or_2 (LE, EQ, LT);
  not not_1 (GT, LE);
  not not_2 (GE, LT);
  Multiplexer #(.select(3)) multiplexer_6 (
    .in0(EQ), .in1(NE), .in2(LT), .in3(LE), .in4(GT), .in5(GE), .out(ConditionCool), .sel(cpu_out[29:27]));  // open: in6, in7

  // Other names for the same wires on the sheet: RZ[15:0] = cpu_out[15:0]; addrB[2:0] = cpu_out[18:16];
  //   B_immediate[3:0] = cpu_out[19:16]; IR[15:0] = cpu_out[31:16]; addrA[2:0] = cpu_out[22:20];
  //   addrC[2:0] = cpu_out[25:23]; Immediate = cpu_out[26]; fun[2:0] = cpu_out[29:27]; Opcode[1:0] = cpu_out[31:30];
  //   PC[15:0] = cpu_out[47:32]

  // Notes on the sheet:
  //   contents of InsMem (hex, n*v repeats v):
  //   493 6d90 2091 491 401 52d 6da0 2122 521 401 15b0 16d0 1621 4540 4e50 1b1 2c91 4e50 3521 2d2 4e50
  //   4d01 21b3 5b1 5b0 4380
endmodule

module ALU (
  input  [15:0] A,
  input  [15:0] B,
  input  [2:0] fun,
  output [15:0] C,
  output negative,
  output zero,
  output carry,
  output overflow
);

  wire and_2_out, and_3_out, and_4_out, and_5_out, Cout_add, Cout_sub, not_2_out, not_3_out, not_4_out,
       not_5_out, not_6_out, not_7_out, or_2_out, or_3_out;
  wire [15:0] AandB, AminusB, AnorB, AorB, AplusB, ASR, LSL, LSR, not_1_out;

  Multiplexer multiplexer_1 (.in0(Cout_add), .in1(Cout_sub), .out(carry), .sel(fun[0]));
  assign not_1_out = ~B;  // NOT_Gate not_1, 16 bits wide
  assign AandB = A & B;  // AND_Gate and_1, 16 bits wide
  assign AorB = A | B;  // OR_Gate or_1, 16 bits wide
  Adder #(.width(16)) adder_1 (.a(A), .b(B), .out(AplusB), .cin(1'b0), .cout(Cout_add));
  Adder #(.width(16)) adder_2 (.a(A), .b(not_1_out), .out(AminusB), .cin(1'b1), .cout(Cout_sub));
  not not_2 (not_2_out, C[15]);
  not not_3 (not_3_out, B[15]);
  not not_4 (not_4_out, A[15]);
  not not_5 (not_5_out, C[15]);
  not not_6 (not_6_out, B[15]);
  not not_7 (not_7_out, A[15]);
  and and_2 (and_2_out, not_2_out, B[15], A[15]);
  and and_3 (and_3_out, C[15], not_3_out, not_4_out);
  and and_4 (and_4_out, not_5_out, not_6_out, A[15]);
  and and_5 (and_5_out, C[15], B[15], not_7_out);
  Shifter #(.width(16)) shifter_1 (.in(A), .\dist (B[3:0]), .out(LSL));
  Shifter #(.shift("lr"), .width(16)) shifter_2 (.in(A), .\dist (B[3:0]), .out(LSR));
  Shifter #(.shift("ar"), .width(16)) shifter_3 (.in(A), .\dist (B[3:0]), .out(ASR));
  assign AnorB = ~(A | B);  // NOR_Gate nor_1, 16 bits wide
  or or_2 (or_2_out, and_2_out, and_3_out);
  or or_3 (or_3_out, and_4_out, and_5_out);
  Multiplexer multiplexer_2 (.in0(or_2_out), .in1(or_3_out), .out(overflow), .sel(fun[0]));
  Multiplexer #(.select(3), .width(16)) multiplexer_3 (
    .in0(AplusB), .in1(AminusB), .in2(AandB), .in3(AorB), .in4(AnorB), .in5(LSL), .in6(LSR), .in7(ASR),
    .out(C), .sel(fun));
  nor nor_2 (zero, C[0], C[1], C[2], C[3], C[4], C[5], C[6], C[7], C[8], C[9], C[10], C[11], C[12], C[13], C[14], C[15]);

  assign negative = C[15];

  // Other names for the same wires on the sheet: B_30[3:0] = B[3:0]; fun_set = fun[0]; Over = overflow

  // Notes on the sheet:
  //   Flags Operations
  //   ALU Operations
endmodule

module RegisterFile (
  input  [2:0] Addr_A,
  input  [2:0] Addr_B,
  input  [2:0] Addr_C,
  input  we,
  input  clk,
  input  reset,
  input  [15:0] C,
  output [15:0] A,
  output [15:0] B
);

  wire dec_R0, dec_R1, dec_R2, dec_R3, dec_R4, dec_R5, dec_R6, dec_R7, we_R0, we_R1, we_R2, we_R3, we_R4,
       we_R5, we_R6, we_R7;
  wire [15:0] R0, R1, R2, R3, R4, R5, R6, R7;

  Decoder #(.enable("false"), .select(3)) decoder_1 (
    .out0(dec_R0), .out1(dec_R1), .out2(dec_R2), .out3(dec_R3), .out4(dec_R4), .out5(dec_R5), .out6(dec_R6),
    .out7(dec_R7), .sel(Addr_C));
  and and_1 (we_R0, dec_R0, we);
  and and_2 (we_R1, dec_R1, we);
  and and_3 (we_R2, dec_R2, we);
  and and_4 (we_R3, dec_R3, we);
  and and_5 (we_R4, dec_R4, we);
  and and_6 (we_R5, dec_R5, we);
  and and_7 (we_R6, dec_R6, we);
  and and_8 (we_R7, dec_R7, we);
  Register #(.width(16)) u_R0 (.D(C), .en(we_R0), .clk(clk), .Q(R0), .clr(reset));
  Register #(.width(16)) u_R1 (.D(C), .en(we_R1), .clk(clk), .Q(R1), .clr(reset));
  Register #(.width(16)) u_R2 (.D(C), .en(we_R2), .clk(clk), .Q(R2), .clr(reset));
  Register #(.width(16)) u_R3 (.D(C), .en(we_R3), .clk(clk), .Q(R3), .clr(reset));
  Register #(.width(16)) u_R4 (.D(C), .en(we_R4), .clk(clk), .Q(R4), .clr(reset));
  Register #(.width(16)) u_R5 (.D(C), .en(we_R5), .clk(clk), .Q(R5), .clr(reset));
  Register #(.width(16)) u_R6 (.D(C), .en(we_R6), .clk(clk), .Q(R6), .clr(reset));
  Register #(.width(16)) u_R7 (.D(C), .en(we_R7), .clk(clk), .Q(R7), .clr(reset));
  Multiplexer #(.select(3), .width(16)) multiplexer_1 (
    .in0(R0), .in1(R1), .in2(R2), .in3(R3), .in4(R4), .in5(R5), .in6(R6), .in7(R7), .out(A), .sel(Addr_A));
  Multiplexer #(.select(3), .width(16)) multiplexer_2 (
    .in0(R0), .in1(R1), .in2(R2), .in3(R3), .in4(R4), .in5(R5), .in6(R6), .in7(R7), .out(B), .sel(Addr_B));

  // Notes on the sheet:
  //   Registers
endmodule

module RegisterFileTester (
  output halt,
  output [15:0] A,
  output [15:0] B,
  output clk
);

  wire undriven;
  wire [2:0] Addr_A_data, Addr_B_data, Addr_C_data;
  wire [3:0] adder_1_out, addr_q;
  wire [15:0] C_data;

  Clock clock_1 (.out(clk));
  ROM #(.addrWidth(4), .dataWidth(3)) Addr_A (.addr(addr_q), .data(Addr_A_data));
  ROM #(.addrWidth(4), .dataWidth(3)) Addr_B (.addr(addr_q), .data(Addr_B_data));
  ROM #(.addrWidth(4), .dataWidth(3)) Addr_C (.addr(addr_q), .data(Addr_C_data));
  ROM #(.addrWidth(4), .dataWidth(1)) we (.addr(addr_q));  // open: data
  ROM #(.addrWidth(4), .dataWidth(16)) C (.addr(addr_q), .data(C_data));
  Adder #(.width(4)) adder_1 (.a(addr_q), .b(4'b0001), .out(adder_1_out), .cin(1'b0));  // open: cout
  Register #(.width(4)) addr (.D(adder_1_out), .en(1'b1), .clk(clk), .Q(addr_q), .clr(1'b0));
  Comparator #(.width(4)) comparator_1 (.a(addr_q), .b(4'b1111), .eq(halt));  // open: gt, lt
  RegisterFile registerfile_1 (
    .Addr_A(Addr_A_data), .Addr_B(Addr_B_data), .Addr_C(Addr_C_data), .we(undriven), .clk(clk), .reset(1'b0),
    .C(C_data), .A(A), .B(B));

  // Notes on the sheet:
  //   contents of Addr_A (hex, n*v repeats v):
  //   5 2 7 3 2 0 2 6 2 4 1 3 5 5 2 6
  //   contents of Addr_B (hex, n*v repeats v):
  //   4 4 6 0 2 3 5 5 5 0 0 4 5 3 7 5
  //   contents of Addr_C (hex, n*v repeats v):
  //   0 5 0 5 5 7 2 3 6 4 0 4 7 7 4 6
  //   contents of we (hex, n*v repeats v):
  //   0 0 0 1 0 0 1 0 0 0 1 1 0 0 1 1
  //   contents of C (hex, n*v repeats v):
  //   1 4 c f 0 5 9 7 c b 9 f b 9 1 e
endmodule

module FSM (
  input  clk,
  input  reset,
  input  [1:0] OPCODE,
  input  ConditionCool,
  output IR_WE,
  output PC_WE,
  output RA_WE,
  output RB_WE,
  output RZ_WE,
  output RD_WE,
  output RW_WE,
  output RF_WE
);

  wire ALUoperation, and_1_out, and_2_out, and_3_out, BranchOperation, LoadOperation, not_1_out, or_1_out,
       or_2_out, StoreOperation, Writeback;
  wire [2:0] adder_1_out, Q, State;

  Decoder #(.enable("false"), .select(2)) decoder_1 (
    .out0(ALUoperation), .out1(BranchOperation), .out2(LoadOperation), .out3(StoreOperation), .sel(OPCODE));
  Register #(.width(3)) register_1 (.D(State), .en(1'b1), .clk(clk), .Q(Q), .clr(or_1_out));
  and and_1 (and_1_out, BranchOperation, ConditionCool, RW_WE);
  or or_1 (or_1_out, and_1_out, reset);
  Adder #(.width(3)) adder_1 (.a(Q), .b(3'b001), .out(adder_1_out));  // open: cin, cout
  not not_1 (not_1_out, adder_1_out[1]);
  and and_2 (and_2_out, adder_1_out[0], not_1_out, adder_1_out[2]);
  and and_3 (and_3_out, RD_WE, ConditionCool, BranchOperation);
  // Probe on State
  Multiplexer #(.width(3)) multiplexer_1 (.in0(adder_1_out), .in1(3'b000), .out(State), .sel(and_2_out));
  Multiplexer multiplexer_2 (.in0(Writeback), .in1(1'b0), .out(RF_WE), .sel(or_2_out));
  or or_2 (or_2_out, BranchOperation, StoreOperation);
  or or_3 (PC_WE, IR_WE, and_3_out);
  Decoder #(.enable("false"), .select(3)) decoder_2 (
    .out0(IR_WE), .out1(RA_WE), .out2(RD_WE), .out3(RW_WE), .out4(Writeback), .sel(Q));  // open: out5, out6, out7

  assign RB_WE = RA_WE;
  assign RZ_WE = RD_WE;

  // Other names for the same wires on the sheet: Cooliness = ConditionCool; Decode = RA_WE; Execute = RD_WE;
  //   Fetch = IR_WE; Memory = RW_WE
endmodule
